// Logisim project Aula1 -  Prática.circ as structural Verilog
module ADD_1 (
  input  A,
  input  B,
  input  Vem_1,
  output out_4,
  output out_5
);

  wire and_1_out, and_2_out, or_1_out, xor_1_out;

  xor xor_1 (xor_1_out, A, B);
  xor xor_2 (out_4, xor_1_out, Vem_1);
  or or_1 (or_1_out, Vem_1, A);
  and and_1 (and_1_out, A, Vem_1);
  and and_2 (and_2_out, or_1_out, B);
  or or_2 (out_5, and_2_out, and_1_out);
endmodule
